# Fritzing sketch piano-5-octave (saved by Fritzing 0.9.3b)
breadboards: 1

parts:
  Part1 = Arduino Uno (Rev3)
  J1 = Piezo Speaker
  R1 = Rotary Potentiometer (Small) [maximum_resistance=100kΩ package=THT]
  S1 = Pushbutton [package="[THT]"]
  S2 = Pushbutton [package="[THT]"]
  S3 = Pushbutton [package="[THT]"]
  S4 = Pushbutton [package="[THT]"]
  S5 = Pushbutton [package="[THT]"]
  S6 = Pushbutton [package="[THT]"]
  S7 = Pushbutton [package="[THT]"]
  R2 = Resistor [tolerance=±5% resistance=10k package=THT]
  R3 = Resistor [tolerance=±5% resistance=10k package=THT]
  R4 = Resistor [tolerance=±5% resistance=10k package=THT]
  R5 = Resistor [tolerance=±5% resistance=10k package=THT]
  R6 = Resistor [tolerance=±5% resistance=10k package=THT]
  R7 = Resistor [tolerance=±5% resistance=10k package=THT]
  R8 = Resistor [tolerance=±5% resistance=10k package=THT]
  R9 = Resistor [tolerance=±5% resistance=10k package=THT]
  R10 = Resistor [tolerance=±5% resistance=220 package=THT]

nets:
  N1: Part1.A0, R1.wiper
  N2: Part1.D8, S7.Pin_1, S7.Pin_2, R2.Pin_0
  N3: Part1.D10_PWM/SS, R10.Pin_1
  N4: Part1.D2, S1.Pin_1, S1.Pin_2, R8.Pin_0
  N5: Part1.D3_PWM, S2.Pin_1, S2.Pin_2, R7.Pin_0
  N6: Part1.D4, S3.Pin_1, S3.Pin_2, R6.Pin_0
  N7: Part1.D5_PWM, S4.Pin_1, S4.Pin_2, R5.Pin_0
  N8: Part1.D6_PWM, S5.Pin_1, S5.Pin_2, R4.Pin_0
  N9: Part1.D7, S6.Pin_1, S6.Pin_2, R3.Pin_0
  N10: Part1.5V, J1.pin1, R1.leg2, R2.Pin_1, R3.Pin_1, R4.Pin_1, R5.Pin_1, R6.Pin_1, R7.Pin_1, R8.Pin_1
  N11: Part1.GND, S1.Pin_3, S1.Pin_4, S2.Pin_3, S2.Pin_4, S3.Pin_3, S3.Pin_4, S4.Pin_3, S4.Pin_4, S5.Pin_3, S5.Pin_4, S6.Pin_3, S6.Pin_4, S7.Pin_3, S7.Pin_4, R9.Pin_1
  N12: J1.pin2, R10.Pin_0
  N13: R1.leg1, R9.Pin_0

// code stored in the sketch: Piano.ino
#define NOTE_C4  262 // DO
#define NOTE_D4  294 // RE
#define NOTE_E4  330 // MI
#define NOTE_F4  349 // FA
#define NOTE_G4  392 // SOL
#define NOTE_A4  440 // LA
#define NOTE_B4  494 // SI

int modificatoreOttava = 1; // Moltiplicatore utilizzato per alzare o abbassare l'ottava riprodotta
const int Speaker = 10; // Il pin dove andrà il buzzer o lo speaker
int Melodia[] = {NOTE_C4, NOTE_D4, NOTE_E4, NOTE_F4, NOTE_G4, NOTE_A4, NOTE_B4};
int Tasto[] = {2, 3, 4, 5, 6, 7, 8}; // I pin dove andranno collegati i 7 pulsanti
int val_Tasto[7]; // Array per la memorizzazione dei valori dei pulsanti



void setup(){
  for(int i=0; i<7; i++){
    pinMode(Tasto[i], INPUT);} // Setta i pulsanti come input
}
 
void loop(){
    
  for(int pin=0; pin<7; pin++){ 
     val_Tasto[pin]=digitalRead(Tasto[pin]);} // Legge lo stato dei pulsanti e li memorizza nell'array val_Tasto[]
      
     modificatoreOttava = map(analogRead(A0),500,1023,1,5); // Assegazione del valore del modificatore in base al potenziometro (5 ottave possibili)
    
    // Se un pulsante è alto, lo speaker, riprodurrà la corrispondente nota musicale  
    if(val_Tasto[0] == HIGH) tone(Speaker, Melodia[0] * modificatoreOttava, 100); // C4 (DO)
    if(val_Tasto[1] == HIGH) tone(Speaker, Melodia[1] * modificatoreOttava, 100); // D4 (RE)
    if(val_Tasto[2] == HIGH) tone(Speaker, Melodia[2] * modificatoreOttava, 100); // E4 (MI)
    if(val_Tasto[3] == HIGH) tone(Speaker, Melodia[3] * modificatoreOttava, 100); // F4 (FA)
    if(val_Tasto[4] == HIGH) tone(Speaker, Melodia[4] * modificatoreOttava, 100); // G4 (SOL)
    if(val_Tasto[5] == HIGH) tone(Speaker, Melodia[5] * modificatoreOttava, 100); // A4 (LA)
    if(val_Tasto[6] == HIGH) tone(Speaker, Melodia[6] * modificatoreOttava, 100); // B4 (SI)
}
